// Logisim project TSD.circ as structural Verilog: 4 circuits, main circuit MCMaq
module MCMaq (
  input  BI,
  input  SPA,
  input  SRS,
  output MT,
  output MM
);

  wire and_1_out, and_2_out, and_3_out, and_4_out, clock_1_out, j_k_ff_1_qn, not_1_out, not_2_out, not_3_out,
       or_1_out;

  Clock clock_1 (.out(clock_1_out));
  not not_1 (not_1_out, SPA);
  not not_2 (not_2_out, SRS);
  not not_3 (not_3_out, BI);
  and and_1 (and_1_out, BI, not_1_out, not_2_out, j_k_ff_1_qn);
  and and_2 (and_2_out, MM, not_1_out, not_3_out);
  and and_3 (and_3_out, MM, SPA);
  and and_4 (and_4_out, MM, SRS);
  or or_1 (or_1_out, and_2_out, and_3_out, and_4_out);
  J_K_Flip_Flop j_k_ff_1 (
    .J(and_1_out), .clk(clock_1_out), .K(or_1_out), .Q(MM), .Qn(j_k_ff_1_qn));  // open: preset, en, reset

  assign MT = MM;
endmodule

module Circuito_Todo (
  input  BI,
  input  SPA,
  input  SRS,
  input  ST,
  output RD,
  output RE,
  output EA
);

  wire mcmaq_1_mm, mcmaq_1_mt;

  MCMaq mcmaq_1 (.BI(BI), .SPA(SRS), .SRS(SPA), .MT(mcmaq_1_mt), .MM(mcmaq_1_mm));
  MM mm_1 (.MMaq(mcmaq_1_mm), .SPA(SPA), .SRS(SRS), .RD(RD), .RE(RE));
  MCT mct_1 (.MMaq(mcmaq_1_mt), .SPA(SPA), .SRS(SRS), .ST(ST), .EA(EA));
endmodule

module MM (
  input  MMaq,
  input  SPA,
  input  SRS,
  output RD,
  output RE
);

  wire and_1_out, and_2_out, and_3_out, and_4_out, and_5_out, and_6_out, and_7_out, and_8_out, and_9_out,
       clock_1_out, D0_q, D0_qn, D1_q, D1_qn, D2_q, D2_qn, not_1_out, not_2_out, not_3_out, not_4_out,
       not_5_out, not_6_out, not_7_out, not_8_out, not_9_out, not_10_out, or_1_out, or_2_out;

  not not_1 (not_1_out, SPA);
  not not_2 (not_2_out, SRS);
  not not_3 (not_3_out, SPA);
  not not_4 (not_4_out, SRS);
  not not_5 (not_5_out, SPA);
  not not_6 (not_6_out, SRS);
  not not_7 (not_7_out, SPA);
  not not_8 (not_8_out, SRS);
  not not_9 (not_9_out, SPA);
  not not_10 (not_10_out, SRS);
  and and_1 (and_1_out, MMaq, not_1_out, not_2_out, D2_qn, D1_q, D0_q);
  and and_2 (and_2_out, MMaq, not_3_out, not_4_out, D2_qn, D1_qn, D0_q);
  and and_3 (and_3_out, MMaq, not_5_out, not_6_out, D2_qn, D1_q, D0_qn);
  and and_4 (and_4_out, MMaq, not_7_out, not_8_out, D2_qn, D0_qn);
  and and_5 (and_5_out, MMaq, not_9_out, not_10_out, D1_qn, D0_qn);
  Clock clock_1 (.out(clock_1_out));
  or or_1 (or_1_out, and_2_out, and_3_out);
  or or_2 (or_2_out, and_4_out, and_5_out);
  D_Flip_Flop D2 (.clk(clock_1_out), .D(and_1_out), .Q(D2_q), .Qn(D2_qn));  // open: preset, en, reset
  D_Flip_Flop D1 (.clk(clock_1_out), .D(or_1_out), .Q(D1_q), .Qn(D1_qn));  // open: preset, en, reset
  D_Flip_Flop D0 (.clk(clock_1_out), .D(or_2_out), .Q(D0_q), .Qn(D0_qn));  // open: preset, en, reset
  and and_6 (and_6_out, D2_qn, D1_qn, D0_q);
  and and_7 (and_7_out, D2_qn, D1_q, D0_qn);
  and and_8 (and_8_out, D2_q, D1_qn, D0_qn);
  and and_9 (and_9_out, D1_q, D2_qn, D0_q);
  or or_3 (RD, and_6_out, and_7_out);
  or or_4 (RE, and_8_out, and_9_out);
endmodule

module MCT (
  input  MMaq,
  input  SPA,
  input  SRS,
  input  ST,
  output EA
);

  wire and_1_out, and_2_out, and_3_out, and_4_out, and_5_out, clock_1_out, not_1_out, not_2_out, not_3_out,
       not_4_out, not_5_out, or_1_out, t_ff_1_qn;

  Clock clock_1 (.out(clock_1_out));
  not not_1 (not_1_out, SPA);
  not not_2 (not_2_out, SRS);
  not not_3 (not_3_out, ST);
  not not_4 (not_4_out, MMaq);
  not not_5 (not_5_out, SRS);
  and and_1 (and_1_out, t_ff_1_qn, MMaq, not_1_out, not_2_out, not_3_out);
  and and_2 (and_2_out, EA, not_4_out);
  and and_3 (and_3_out, EA, MMaq, SPA);
  and and_4 (and_4_out, EA, MMaq, SRS);
  and and_5 (and_5_out, EA, MMaq, not_5_out, ST);
  T_Flip_Flop t_ff_1 (.clk(clock_1_out), .T(or_1_out), .Q(EA), .Qn(t_ff_1_qn));  // open: preset, reset, en
  or or_1 (or_1_out, and_1_out, and_2_out, and_3_out, and_4_out, and_5_out);
endmodule
